# Fritzing sketch OpenBB-8 (saved by Fritzing 0.9.3b)
circuit board: 8.46667cm x 5.64444cm
breadboards: 1

parts:
  part = Arduino Uno (Rev3)
  part_2 = L293D [package=THT]
  part_3 = DC Motor
  part_4 = DC Motor
  part_5 = Battery block 9V
  part_6 = Bluetooth HC-05 Macho

nets:
  N1: part.D9_PWM, part_2.In_2
  N2: part.D10_PWM/SS, part_2.In_1
  N3: part.D0/RX, part_6.TXD
  N4: part.D1/TX, part_6.RXD
  N5: part.D5_PWM, part_2.In_3
  N6: part.D6_PWM, part_2.In_4
  5V: part.5V, part_2.Enable_1, part_2.Enable_2, part_2.+V, part_6.VCC
  GND: part.GND, part_2.0V, part_5.-, part_6.GND
  N7: part.VIN, part_2.+Vmotor, part_5.+
  N8: part_2.Out_1_(_Controlled_by_Enable_1_), part_3.pin_2
  N9: part_2.Out_2_(_Controlled_by_Enable_1_), part_3.pin_1
  N10: part_2.Out_3_(_Controlled_by_Enable_2_), part_4.pin_2
  N11: part_2.Out_4_(_Controlled_by_Enable_2_), part_4.pin_1

// code stored in the sketch: Untitled2.ino

/*


  OpenBB-8 PoC code

  Open source BB-8 project

  

  Project made by:

  - Alain Flores Temblador

  - Carlos Alberto R. de León Quezada

  - Daniel Hernández Muñoz

  - Oscar Jesús de la Torre Martínez

  

  This project was published under the GNU General Public License 3.0

  More info in https://github.com/lordfriky/OpenBB-8/blob/master/LICENSE

*/



char dataIn='S';      // Declaration of bluetooth variables

char determinant;     // We just need one, but TechBuilder made it like this

char det;



int vel = 250;        // Initial speed



void setup(){

  Serial.begin(9600);

                        //Declaration of both motors

  pinMode(5, OUTPUT);     //Left motor

  pinMode(6, OUTPUT);

  pinMode(9, OUTPUT);     //Right motor

  pinMode(10, OUTPUT);



}



void loop(){

  det = check();

  

/*  

  Anatomy of the movement function:

  There's 2 motors, left (5 & 6) and right (9 & 10)

  The first 2 'analogWrite' belogs to left motor, the next ones to the right

  The first line of both motors belongs to the front, the next ones to the back

  So if we set both of the first lines of the motors the BB-8 is going to move to the front

  And vice versa

  If we divide the 'vel' value we can move the BB-8 in a diagonal

  

  And that's all the basic info you need to know to understant the code

*/

  

  while (det == 'F'){   // F, forward

    analogWrite(5, vel);

    analogWrite(6, 0);

    analogWrite(9, vel);

    analogWrite(10, 0);

    

    det = check();

  }

  

  while (det == 'B'){   // B, back

    analogWrite(5, 0);

    analogWrite(6, vel);

    analogWrite(9, 0);

    analogWrite(10, vel);

    

    det = check();

  }



  while (det == 'L'){   // L, left rotation

    analogWrite(5, 0);

    analogWrite(6, vel);

    analogWrite(9, vel);

    analogWrite(10, 0);

    

    det = check();

  }

  

  while (det == 'R'){   // R, right rotation

    analogWrite(5, vel);

    analogWrite(6, 0);

    analogWrite(9, 0);

    analogWrite(10, vel);

    

    det = check();

  }

  

  while (det == 'I'){   // I, northeast

    analogWrite(5, vel);

    analogWrite(6, 0);

    analogWrite(9, vel/2);

    analogWrite(10, 0);

    

    det = check();

  }

  

  while (det == 'J'){   // J, southeast

    analogWrite(5, 0);

    analogWrite(6, vel);

    analogWrite(9, 0);

    analogWrite(10, vel/2);

    

    det = check();

  }  

  

  while (det == 'G'){   // G, northwest

    analogWrite(5, vel/2);

    analogWrite(6, 0);

    analogWrite(9, vel);

    analogWrite(10, 0);

    

    det = check();

  }

  

  while (det == 'H'){   // H, southwest

    analogWrite(5, 0);

    analogWrite(6, vel/2);

    analogWrite(9, 0);

    analogWrite(10, vel);

    

    det = check();

  }  

  

  while (det == 'S'){   // S, stop

    analogWrite(5, 0);

    analogWrite(6, 0);

    analogWrite(9, 0);

    analogWrite(10, 0);

    

    det = check();

  }

}



int check(){                  // Bluetooth read function (not really needed, btw...)

  if (Serial.available() > 0){// I'm just following the TechBuilder code

    dataIn = Serial.read(); 

    

    //-------- DIRECTION --------//

    

    if (dataIn == 'F'){

      determinant = 'F';      // Forward

    } 

    else if (dataIn == 'B'){

      determinant = 'B';      // Back

    }

    else if (dataIn == 'L'){

      determinant = 'L';      // Left Rotation

    }

    else if (dataIn == 'R'){

      determinant = 'R';      // Right Rotation

    }

    else if (dataIn == 'I'){

      determinant = 'I';      // Northeast

    } 

    else if (dataIn == 'J'){

      determinant = 'J';      // Southeast

    }

    else if (dataIn == 'G'){

      determinant = 'G';      // Northwest

    }   

    else if (dataIn == 'H'){

      determinant = 'H';      // Southwest

      

    }

    else if (dataIn == 'S'){

      determinant = 'S';      // Stop

    }

    

    //---------- SPEED ----------//

    

    else if (dataIn == '0'){

      vel = 250;              // Max Speed

    }

    else if (dataIn == '1'){

      vel = 174;              // Mid Speed

    }

    else if (dataIn == '2'){

      vel = 86;               // Min Speed

    }

  }

  return determinant;         // Set check() value as  determinant

}
